# Fritzing sketch PoolController (saved by Fritzing 0.9.5d)
circuit board: 9.09797cm x 6.87cm
breadboards: 1

parts:
  part = shrouded pin header, 40 pins [form="♂ (shrouded male)"]
  485MAX = female pin header, 4 pins [form="♀ (female)"]
  Temp_3 = Screw terminal - 2 pins [package=THT]
  Temp_2 = Screw terminal - 2 pins [package=THT]
  Temp_1 = Screw terminal - 2 pins [package=THT]
  10K = Resistor [tolerance=±5% resistance=10k package=THT]
  10K_2 = Resistor [tolerance=±5% resistance=10k power=0.25W package=THT]
  10K_3 = Resistor [tolerance=±5% resistance=10k power=0.25W package=THT]
  10K_4 = Resistor [tolerance=±5% resistance=10k power=0.25W package=THT]
  PWR = Screw terminal - 2 pins [package=THT]
  Temp_4 = Screw terminal - 2 pins [package=THT]
  J2 = female pin header, 4 pins [form="♀ (female)"]
  ADS1115 = female pin header, 10 pins [form="♀ (female)"]
  Relay = female pin header, 6 pins [form="♀ (female)"]

nets:
  N1: part.pin4, 10K.Pin_1, 10K_2.Pin_1, 10K_3.Pin_1, 10K_4.Pin_1, J2.pin1, Relay.pin1
  N2: part.pin7, Relay.pin2
  N3: part.pin8, Relay.pin3
  N4: part.pin9, Relay.pin4
  N5: part.pin10, Relay.pin5
  N6: part.pin15, 485MAX.pin2, 485MAX.pin3
  N7: part.pin16, 485MAX.pin4
  N8: part.pin17, 485MAX.pin1
  N9: part.pin19, part.pin20, Temp_3.pin2, Temp_2.pin2, Temp_1.pin2, Temp_4.pin2, J2.pin4, Relay.pin6
  N10: part.pin21, ADS1115.pin1
  N11: part.pin23, ADS1115.pin4
  N12: part.pin24, ADS1115.pin3
  N13: Temp_3.pin1, 10K_3.Pin_0, ADS1115.pin9
  N14: Temp_2.pin1, 10K_2.Pin_0, ADS1115.pin8
  N15: Temp_1.pin1, 10K.Pin_0, ADS1115.pin7
  N16: 10K_4.Pin_0, Temp_4.pin1, ADS1115.pin10
  N17: PWR.pin1, ADS1115.pin2

notes:
  Raspberry
  1
  GND
  5v
  G
  Y
  40
  5v 4 3 2 1 Gnd
  VDD
  SCL
  SDA
  A3
  A0
  A2
  A1
  Pool Controller
  by Morten Nielsen
